# Fritzing sketch esquema conexión raspberrypi tmp36 (saved by Fritzing 0.8.3b)
breadboards: 1

parts:
  U1 = TMP36 [package=to-92-kit]
  Raspberry_Pi_rev1 = Raspberry Pi rev1
  IC1 = MCP3008 8-channel 10-bit ADC [part_number=MCP3008]

nets:
  VCC: U1.VCC, Raspberry_Pi_rev1.3V3, Raspberry_Pi_rev1.GIPO_0, Raspberry_Pi_rev1.GIPO_1, IC1.no_name_yet#15, IC1.no_name_yet#16
  N1: U1.VOUT, IC1.no_name_yet#1
  GND: U1.GND, Raspberry_Pi_rev1.GND, Raspberry_Pi_rev1.GPIO_14, Raspberry_Pi_rev1.GPIO_18, Raspberry_Pi_rev1.GPIO_24, IC1.no_name_yet#9, IC1.no_name_yet#11, IC1.no_name_yet#13, IC1.no_name_yet#14
  N2: Raspberry_Pi_rev1.GPIO4, IC1.no_name_yet#12
  N3: Raspberry_Pi_rev1.GPIO_25, Raspberry_Pi_rev1.GPIO_8, IC1.no_name_yet#10

notes:
  CLK BLANCO GPIO 18 12 1
  DIN GRIS GPIO 23 16 4
  DOUT VERDE GPIO 24 18 5
  CS AMARILLO GPIO 25 22 6
  PATILLA MCP3008
  COLOR CABLE
  NÚMERO GPIO EN PLACA RASPBERRY PI
  NÚMERO HEADER 1-26
  NÚMERO PIN EN QUICK2WIRE (SOC PIN NUMBER)
